// Logisim project CustomizedManoMachine.circ as structural Verilog: 19 circuits, main circuit CPU
module CPU (
  input  [3:0] INPR,
  output out_2,
  output out_3,
  output out_4,
  output out_5,
  output out_6,
  output out_7,
  output out_8,
  output out_9,
  output out_10,
  output out_11,
  output out_12,
  output out_13,
  output out_14,
  output out_15,
  output out_16,
  output out_17,
  output out_18,
  output out_19,
  output out_20,
  output out_21,
  output out_22,
  output out_23,
  output [3:0] out_24
);

  wire Clk, clock_1_out, E_Out, m_1_ld, m_1_str, S;
  wire [3:0] AC, AR, DR, n4_bit_alu_1_alu_output, pc_1_out_9;
  wire [7:0] bus_1_output, IR, ram_1_data;

  Clock_part clock_1 (.out(clock_1_out));
  Clock clock_2 (.Pulse(clock_1_out), .S(S), .Clk(Clk));
  _4_bit_alu u_4_bit_alu_1 (
    .AC(AC), .DR(DR), .Input_E(out_18), .INPR(INPR), .ALU_Output(n4_bit_alu_1_alu_output), .Output_E(E_Out),
    .T3(out_20), .T4(out_19), .D13(out_4), .D12(out_5), .D11(out_6), .D10(out_7), .D9(out_8), .D7(out_10),
    .D2(out_15), .D1(out_16), .D0(out_17));
  M m_1 (
    .T3(out_20), .T1(out_22), .D6(out_11), .D5(out_12), .D2(out_15), .D3(out_14), .D1(out_16), .D0(out_17),
    .str(m_1_str), .LD(m_1_ld));
  PC pc_1 (
    .Input(bus_1_output[3:0]), .out_9(pc_1_out_9), .T4(out_19), .T3(out_20), .T1(out_22), .D6(out_11),
    .D5(out_12), .D4(out_13), .CLK(Clk));
  IR ir_1 (.in_3(bus_1_output), .out_4(IR), .T1(out_22), .CLK(Clk));
  OUTR outr_1 (.D14(out_3), .T3(out_20), .in_4(bus_1_output[3:0]), .out_5(out_24), .CLK(Clk));
  AR ar_1 (.in_6(bus_1_output[3:0]), .out_7(AR), .T3(out_20), .T2(out_21), .T0(out_23), .D5(out_12), .CLK(Clk));
  DR dr_1 (.T3(out_20), .D2(out_15), .D1(out_16), .D0(out_17), .in_2(bus_1_output[3:0]), .out_7(DR), .CLK(Clk));
  // Probe on out_24
  Control_Unit control_unit_1 (
    .IR_4_7(IR[7:4]),
    .D_i({out_2, out_3, out_4, out_5, out_6, out_7, out_8, out_9, out_10, out_11, out_12, out_13, out_14, out_15, out_16, out_17}),
    .T_i({out_19, out_20, out_21, out_22, out_23}), .Flip_flop_out({out_18, S}), .Clk(Clk), .E_Carry(E_Out),
    .SC_INPUT(4'b0000));
  // Probe on DR
  AC ac_1 (
    .in_2(n4_bit_alu_1_alu_output), .out_14(AC), .T4(out_19), .D10(out_7), .D13(out_4), .D12(out_5),
    .D11(out_6), .D9(out_8), .D2(out_15), .D1(out_16), .D0(out_17), .T3(out_20), .D7(out_10), .CLK(Clk));
  RAM #(.addrWidth(4), .bus("separate")) ram_1 (
    .addr(AR), .din(bus_1_output), .data(ram_1_data), .str(m_1_str), .clk(Clk), .ld(m_1_ld));  // open: sel, clr
  // Probe on AR
  // Probe on pc_1_out_9
  // Probe on IR
  // Probe on AC
  // Probe on AC
  Bus bus_1 (
    .PC(pc_1_out_9), .AC(AC), .AR(AR), .IR(IR), .M(ram_1_data), .Output(bus_1_output), .T4(out_19),
    .T2(out_21), .T1(out_22), .T0(out_23), .D6(out_11), .D5(out_12), .D4(out_13), .D3(out_14), .D2(out_15),
    .D1(out_16), .D14(out_3), .D0(out_17), .T3(out_20));

  // Other names for the same wires on the sheet: D0 = out_17; D1 = out_16; D2 = out_15; D3 = out_14; D4 = out_13;
  //   D5 = out_12; D6 = out_11; D7 = out_10; D8 = out_9; D9 = out_8; D10 = out_7; D11 = out_6; D12 = out_5;
  //   D13 = out_4; D14 = out_3; D15 = out_2; T0 = out_23; T1 = out_22; T2 = out_21; T3 = out_20; T4 = out_19;
  //   E = out_18
endmodule

module Bus (
  input  [3:0] AR,
  input  [3:0] PC,
  input  [3:0] AC,
  input  [7:0] IR,
  input  [7:0] M,
  input  T4,
  input  T3,
  input  T2,
  input  T1,
  input  T0,
  input  D14,
  input  D6,
  input  D5,
  input  D4,
  input  D3,
  input  D2,
  input  D1,
  input  D0,
  output [7:0] Output
);

  wire and_1_out, and_2_out, and_3_out, and_4_out, and_5_out, and_6_out, and_7_out, and_8_out, and_9_out, S0,
       S1, S2, x1, x2, x4, x7;

  and and_1 (and_1_out, D4, T3);
  and and_2 (and_2_out, D5, T4);
  and and_3 (and_3_out, T3, D5);
  or u_AR (x1, and_1_out, and_2_out);
  or u_PC (x2, T0, and_3_out);
  and and_4 (and_4_out, D3, T3);
  or u_AC (x4, and_4_out, and_5_out);
  and and_5 (and_5_out, D14, T3);
  and and_6 (and_6_out, D0, T3);
  and and_7 (and_7_out, D1, T3);
  and and_8 (and_8_out, D2, T3);
  and and_9 (and_9_out, D6, T3);
  or MEM (x7, T1, and_6_out, and_7_out, and_8_out, and_9_out);
  Priority_Encoder priority_encoder_1 (
    .in0(1'b0), .in1(x1), .in2(x2), .in3(1'b0), .in4(x4), .in5(T2), .in6(1'b0), .in7(x7), .out({S2, S1, S0}));  // open: en_in
  Multiplexer #(.select(3), .width(8), .enable("false")) multiplexer_1 (
    .in0({8{1'b0}}), .in1({4'b0000, AR}), .in2({4'b0000, PC}), .in3({8{1'b0}}), .in4({4'b0000, AC}),
    .in5(IR), .in6({8{1'b0}}), .in7(M), .out(Output), .sel({S2, S1, S0}));

  // Other names for the same wires on the sheet: Out[7:0] = Output; x5 = T2

  // Notes on the sheet:
  //   IR
endmodule

module Clock (
  input  Pulse,
  input  S,
  output Clk
);

  wire d_ff_1_qn;

  D_Flip_Flop d_ff_1 (.clk(Pulse), .D(S), .Qn(d_ff_1_qn));  // open: Q, preset, en, reset
  and and_1 (Clk, Pulse, d_ff_1_qn);
endmodule

module Control_Unit (
  input  [3:0] IR_4_7,
  input  [3:0] SC_INPUT,
  input  Clk,
  input  E_Carry,
  output [15:0] D_i,
  output [4:0] T_i,
  output [1:0] Flip_flop_out
);

  wire [3:0] sc_1_out_12;

  SC sc_1 (
    .T4(T_i[4]), .T3(T_i[3]), .D6(D_i[6]), .D5(D_i[5]), .D4(D_i[4]), .D3(D_i[3]), .D2(D_i[2]), .D1(D_i[1]),
    .D0(D_i[0]), .in_2(SC_INPUT), .out_12(sc_1_out_12), .CLK(Clk));
  Decoder #(.select(4), .enable("false")) decoder_1 (
    .out0(D_i[0]), .out1(D_i[1]), .out2(D_i[2]), .out3(D_i[3]), .out4(D_i[4]), .out5(D_i[5]), .out6(D_i[6]),
    .out7(D_i[7]), .out8(D_i[8]), .out9(D_i[9]), .out10(D_i[10]), .out11(D_i[11]), .out12(D_i[12]),
    .out13(D_i[13]), .out14(D_i[14]), .out15(D_i[15]), .sel(IR_4_7));
  E e_1 (
    .CLK(Clk), .out_9(Flip_flop_out[1]), .D12(D_i[12]), .D11(D_i[11]), .E_Out(E_Carry), .D8(D_i[8]),
    .T4(T_i[4]), .D1(D_i[1]), .T3(T_i[3]));
  Decoder #(.select(4), .enable("false")) decoder_2 (
    .out0(T_i[0]), .out1(T_i[1]), .out2(T_i[2]), .out3(T_i[3]), .out4(T_i[4]), .sel(sc_1_out_12));  // open: out5, out6, out7, out8, out9, out10, out11, out12, out13, out14, out15
  S S (.CLK(Clk), .D15(D_i[15]), .T3(T_i[3]), .out_4(Flip_flop_out[0]));

  // Other names for the same wires on the sheet: D0 = D_i[0]; D1 = D_i[1]; D2 = D_i[2]; D3 = D_i[3]; D4 = D_i[4];
  //   D5 = D_i[5]; D6 = D_i[6]; D7 = D_i[7]; D8 = D_i[8]; D9 = D_i[9]; D10 = D_i[10]; D11 = D_i[11]; D12 = D_i[12];
  //   D13 = D_i[13]; D14 = D_i[14]; D15 = D_i[15]; S = Flip_flop_out[0]; E = Flip_flop_out[1]; T0 = T_i[0];
  //   T1 = T_i[1]; T2 = T_i[2]; T3 = T_i[3]; T4 = T_i[4]

  // Notes on the sheet:
  //   Operation Decoder
  //   Sequence Counter
  //   Timing Decoder
endmodule

module M (
  input  T3,
  input  T1,
  input  D6,
  input  D5,
  input  D3,
  input  D2,
  input  D1,
  input  D0,
  output LD,
  output str
);

  wire and_1_out, and_2_out, and_3_out, and_4_out, and_5_out, and_6_out;

  and and_1 (and_1_out, D0, T3);
  and and_2 (and_2_out, D1, T3);
  and and_3 (and_3_out, D2, T3);
  and and_4 (and_4_out, D6, T3);
  and and_5 (and_5_out, D3, T3);
  and and_6 (and_6_out, D5, T3);
  or or_1 (LD, T1, and_1_out, and_2_out, and_3_out, and_4_out);
  or or_2 (str, and_5_out, and_6_out);
endmodule

module AR (
  input  CLK,
  input  T3,
  input  T2,
  input  T0,
  input  D5,
  input  [3:0] in_6,
  output [3:0] out_7
);

  wire INR, LD;

  and u_INR (INR, D5, T3);
  or u_LD (LD, T0, T2);
  _4_bit_register u_4_bit_register_1 (.INPUT(in_6), .CLK(CLK), .OUTPUT(out_7), .LD(LD), .INC(INR));  // open: CLR

  // Other names for the same wires on the sheet: In[3:0] = in_6; Out[3:0] = out_7
endmodule

module PC (
  input  CLK,
  input  [3:0] Input,
  input  T4,
  input  T3,
  input  T1,
  input  D6,
  input  D5,
  input  D4,
  output [3:0] out_9
);

  wire and_1_out, and_2_out, LD, or_1_out;

  or or_1 (or_1_out, D6, D4);
  and and_1 (and_1_out, or_1_out, T3);
  and and_2 (and_2_out, D5, T4);
  or or_2 (LD, and_1_out, and_2_out);
  _4_bit_register u_4_bit_register_1 (.INPUT(Input), .CLK(CLK), .OUTPUT(out_9), .LD(LD), .INC(T1));  // open: CLR

  // Other names for the same wires on the sheet: In[3:0] = Input; INR = T1; Out[3:0] = out_9
endmodule

module DR (
  input  CLK,
  input  [3:0] in_2,
  input  T3,
  input  D2,
  input  D1,
  input  D0,
  output [3:0] out_7
);

  wire ADD_out, AND_out, LD, LDA_out;

  and AND (AND_out, D0, T3);
  and ADD (ADD_out, D1, T3);
  and LDA (LDA_out, D2, T3);
  or u_LD (LD, AND_out, ADD_out, LDA_out);
  _4_bit_register u_4_bit_register_1 (.INPUT(in_2), .CLK(CLK), .OUTPUT(out_7), .LD(LD));  // open: INC, CLR

  // Other names for the same wires on the sheet: In[3:0] = in_2; Out[3:0] = out_7
endmodule

module AC (
  input  CLK,
  input  [3:0] in_2,
  input  T3,
  input  T4,
  input  D13,
  input  D12,
  input  D11,
  input  D10,
  input  D9,
  input  D7,
  input  D2,
  input  D1,
  input  D0,
  output [3:0] out_14
);

  wire ADD_out, AND_out, CIL_out, CIR_out, CLR, CMA_out, DR_out, INPR_out, INR, LD;

  and u_CLR (CLR, D7, T3);
  and u_INR (INR, D10, T3);
  and AND (AND_out, D0, T4);
  and ADD (ADD_out, D1, T4);
  and DR (DR_out, D2, T4);
  and CMA (CMA_out, D9, T3);
  and CIR (CIR_out, D11, T3);
  and CIL (CIL_out, D12, T3);
  and INPR (INPR_out, D13, T3);
  or u_LD (LD, AND_out, ADD_out, DR_out, CMA_out, CIR_out, CIL_out, INPR_out);
  _4_bit_register u_4_bit_register_1 (.INPUT(in_2), .CLK(CLK), .OUTPUT(out_14), .LD(LD), .INC(INR), .CLR(CLR));

  // Other names for the same wires on the sheet: In[3:0] = in_2; Out[3:0] = out_14
endmodule

module _1_bit_alu (
  input  INPR,
  input  DR,
  input  AC,
  input  AND,
  input  CIN,
  input  ADD,
  input  LD_DR,
  input  COMP,
  input  LD_INPR,
  input  SHR,
  input  SHL,
  input  AC_I_1,
  input  AC_I_1_2,
  output COUT,
  output OUTAC
);

  wire ADD_out, adder_1_out, and_1_out, AND_2_out, COMP_out, LD_DR_out, LD_INPR_out, not_1_out, SHL_out,
       SHR_out;

  Adder #(.width(1)) adder_1 (.a(AC), .b(DR), .out(adder_1_out), .cin(CIN), .cout(COUT));
  not not_1 (not_1_out, AC);
  and and_1 (and_1_out, AC, DR);
  and AND_2 (AND_2_out, AND, and_1_out);
  and u_ADD (ADD_out, ADD, adder_1_out);
  and u_LD_DR (LD_DR_out, LD_DR, DR);
  and u_COMP (COMP_out, COMP, not_1_out);
  and u_LD_INPR (LD_INPR_out, LD_INPR, INPR);
  and u_SHR (SHR_out, SHR, AC_I_1_2);
  and u_SHL (SHL_out, SHL, AC_I_1);
  or or_1 (OUTAC, AND_2_out, ADD_out, LD_DR_out, COMP_out, LD_INPR_out, SHR_out, SHL_out);
endmodule

// ALU
module _4_bit_alu (
  input  Input_E,
  input  [3:0] AC,
  input  [3:0] INPR,
  input  [3:0] DR,
  input  T3,
  input  T4,
  input  D13,
  input  D12,
  input  D11,
  input  D10,
  input  D9,
  input  D7,
  input  D2,
  input  D1,
  input  D0,
  output Output_E,
  output [3:0] ALU_Output
);

  wire ADD_CTRL, and_1_out, and_2_out, and_3_out, AND_CTRL, COM_CTRL, DR_CTRL, E_Carry, INPR_CTRL,
       n1_bit_alu_1_cout, n1_bit_alu_2_cout, n1_bit_alu_3_cout, SHL_CTRL, SHR_CTRL;

  _1_bit_alu u_1_bit_alu_1 (
    .AND(AND_CTRL), .ADD(ADD_CTRL), .LD_DR(DR_CTRL), .COMP(COM_CTRL), .LD_INPR(INPR_CTRL), .SHR(SHR_CTRL),
    .SHL(SHL_CTRL), .AC_I_1(Input_E), .AC_I_1_2(AC[1]), .OUTAC(ALU_Output[0]), .INPR(INPR[0]), .DR(DR[0]),
    .AC(AC[0]), .CIN(1'b0), .COUT(n1_bit_alu_1_cout));
  _1_bit_alu u_1_bit_alu_2 (
    .AND(AND_CTRL), .ADD(ADD_CTRL), .LD_DR(DR_CTRL), .COMP(COM_CTRL), .LD_INPR(INPR_CTRL), .SHR(SHR_CTRL),
    .SHL(SHL_CTRL), .AC_I_1(AC[0]), .AC_I_1_2(AC[2]), .OUTAC(ALU_Output[1]), .INPR(INPR[1]), .DR(DR[1]),
    .AC(AC[1]), .CIN(n1_bit_alu_1_cout), .COUT(n1_bit_alu_2_cout));
  and and_1 (and_1_out, AC[3], SHL_CTRL);
  or or_1 (Output_E, and_1_out, and_2_out, and_3_out);
  and and_2 (and_2_out, AC[0], SHR_CTRL);
  and and_3 (and_3_out, E_Carry, ADD_CTRL);
  _1_bit_alu u_1_bit_alu_3 (
    .AND(AND_CTRL), .ADD(ADD_CTRL), .LD_DR(DR_CTRL), .COMP(COM_CTRL), .LD_INPR(INPR_CTRL), .SHR(SHR_CTRL),
    .SHL(SHL_CTRL), .AC_I_1(AC[1]), .AC_I_1_2(AC[3]), .OUTAC(ALU_Output[2]), .INPR(INPR[2]), .DR(DR[2]),
    .AC(AC[2]), .CIN(n1_bit_alu_2_cout), .COUT(n1_bit_alu_3_cout));
  _1_bit_alu u_1_bit_alu_4 (
    .AND(AND_CTRL), .ADD(ADD_CTRL), .LD_DR(DR_CTRL), .COMP(COM_CTRL), .LD_INPR(INPR_CTRL), .SHR(SHR_CTRL),
    .SHL(SHL_CTRL), .AC_I_1(AC[2]), .AC_I_1_2(Input_E), .OUTAC(ALU_Output[3]), .INPR(INPR[3]), .DR(DR[3]),
    .AC(AC[3]), .CIN(n1_bit_alu_3_cout), .COUT(E_Carry));
  and and_4 (AND_CTRL, D0, T4);
  and and_5 (ADD_CTRL, D1, T4);
  and and_6 (DR_CTRL, D2, T4);
  and and_7 (INPR_CTRL, D13, T3);
  and and_8 (COM_CTRL, D9, T3);
  and and_9 (SHR_CTRL, D11, T3);
  and and_10 (SHL_CTRL, D12, T3);

  // Other names for the same wires on the sheet: I0 = ALU_Output[0]; I1 = ALU_Output[1]; I2 = ALU_Output[2];
  //   I3 = ALU_Output[3]; E = Input_E
endmodule

module IR (
  input  CLK,
  input  T1,
  input  [7:0] in_3,
  output [7:0] out_4
);

  _8_bit_register u_8_bit_register_1 (.LD(T1), .in_2(in_3), .CLK(CLK), .out_4(out_4));

  // Other names for the same wires on the sheet: In[7:0] = in_3; LD = T1; Out[7:0] = out_4
endmodule

module OUTR (
  input  CLK,
  input  D14,
  input  T3,
  input  [3:0] in_4,
  output [3:0] out_5
);

  wire LD;

  and u_LD (LD, T3, D14);
  _4_bit_register u_4_bit_register_1 (.INPUT(in_4), .CLK(CLK), .OUTPUT(out_5), .LD(LD));  // open: INC, CLR

  // Other names for the same wires on the sheet: In[3:0] = in_4; Out[3:0] = out_5
endmodule

module INPR (
  input  CLK,
  input  [3:0] in_2,
  output [3:0] out_3
);

  _4_bit_register u_4_bit_register_1 (.INPUT(in_2), .CLK(CLK), .OUTPUT(out_3));  // open: LD, INC, CLR

  // Other names for the same wires on the sheet: In[3:0] = in_2; Out[3:0] = out_3
endmodule

module SC (
  input  CLK,
  input  [3:0] in_2,
  input  T4,
  input  T3,
  input  D6,
  input  D5,
  input  D4,
  input  D3,
  input  D2,
  input  D1,
  input  D0,
  output [3:0] out_12
);

  wire and_1_out, and_2_out, and_3_out, and_4_out, and_5_out, and_6_out, and_7_out, CLR, not_1_out;

  and and_1 (and_1_out, D0, T4);
  and and_2 (and_2_out, D1, T4);
  and and_3 (and_3_out, D2, T4);
  and and_4 (and_4_out, D3, T3);
  and and_5 (and_5_out, D4, T3);
  and and_6 (and_6_out, D5, T4);
  and and_7 (and_7_out, D6, T3);
  or u_CLR (CLR, and_1_out, and_2_out, and_3_out, and_4_out, and_5_out, and_6_out, and_7_out);
  Counter #(.width(4), .max('hf)) counter_1 (
    .load(CLR), .D(in_2), .count(not_1_out), .Q(out_12), .clk(CLK));  // open: carry, clr
  not not_1 (not_1_out, CLR);

  // Other names for the same wires on the sheet: In[3:0] = in_2; Out[3:0] = out_12
endmodule

module E (
  input  CLK,
  input  E_Out,
  input  T3,
  input  T4,
  input  D12,
  input  D11,
  input  D8,
  input  D1,
  output out_9
);

  wire and_3_out, CLR, EBit, ECarry, not_1_out, or_1_out, Reset, Set, UpdE;

  and and_1 (Set, UpdE, E_Out);
  and u_CLR (CLR, T3, D8);
  or or_1 (or_1_out, D11, D12);
  and and_2 (EBit, T3, or_1_out);
  and and_3 (and_3_out, UpdE, not_1_out);
  not not_1 (not_1_out, E_Out);
  or or_2 (Reset, CLR, and_3_out);
  and u_ECarry (ECarry, D1, T4);
  or u_UpdE (UpdE, ECarry, EBit);
  J_K_Flip_Flop j_k_ff_1 (.J(Set), .clk(CLK), .K(Reset), .Q(out_9));  // open: Qn, preset, en, reset

  // Other names for the same wires on the sheet: New_E = E_Out
endmodule

module S (
  input  CLK,
  input  D15,
  input  T3,
  output out_4
);

  wire SET;

  and and_1 (SET, D15, T3);
  J_K_Flip_Flop j_k_ff_1 (.J(SET), .clk(CLK), .K(1'b0), .Q(out_4));  // open: Qn, preset, en, reset
endmodule

module _4_bit_register (
  input  INC,
  input  LD,
  input  [3:0] INPUT,
  input  CLK,
  input  CLR,
  output [3:0] OUTPUT
);

  wire and_1_out, and_2_out, and_3_out, and_4_out, and_5_out, and_6_out, and_7_out, and_8_out, and_9_out,
       and_10_out, and_11_out, and_12_out, not_1_out, not_2_out, not_3_out, not_4_out, not_5_out, not_6_out,
       or_1_out, or_2_out, or_3_out, or_4_out, or_5_out, or_6_out, or_7_out, or_8_out;

  not not_1 (not_1_out, LD);
  and and_1 (and_1_out, INC, not_1_out);
  not not_2 (not_2_out, not_1_out);
  not not_3 (not_3_out, INPUT[0]);
  not not_4 (not_4_out, INPUT[1]);
  not not_5 (not_5_out, INPUT[2]);
  not not_6 (not_6_out, INPUT[3]);
  and and_2 (and_2_out, not_2_out, INPUT[0]);
  and and_3 (and_3_out, not_2_out, not_3_out);
  and and_4 (and_4_out, not_2_out, INPUT[1]);
  and and_5 (and_5_out, not_2_out, not_4_out);
  and and_6 (and_6_out, not_2_out, INPUT[2]);
  and and_7 (and_7_out, not_2_out, not_5_out);
  and and_8 (and_8_out, not_2_out, INPUT[3]);
  and and_9 (and_9_out, not_2_out, not_6_out);
  and and_10 (and_10_out, and_1_out, OUTPUT[0]);
  and and_11 (and_11_out, and_1_out, OUTPUT[0], OUTPUT[1]);
  and and_12 (and_12_out, and_1_out, OUTPUT[0], OUTPUT[1], OUTPUT[2]);
  or or_1 (or_1_out, and_2_out, and_1_out);
  or or_2 (or_2_out, and_3_out, and_1_out);
  or or_3 (or_3_out, and_4_out, and_10_out);
  or or_4 (or_4_out, and_10_out, and_5_out);
  or or_5 (or_5_out, and_6_out, and_11_out);
  or or_6 (or_6_out, and_11_out, and_7_out);
  or or_7 (or_7_out, and_8_out, and_12_out);
  or or_8 (or_8_out, and_12_out, and_9_out);
  J_K_Flip_Flop j_k_ff_1 (.J(or_1_out), .clk(CLK), .K(or_2_out), .Q(OUTPUT[0]), .reset(CLR));  // open: Qn, preset, en
  J_K_Flip_Flop j_k_ff_2 (.J(or_3_out), .clk(CLK), .K(or_4_out), .Q(OUTPUT[1]), .reset(CLR));  // open: Qn, preset, en
  J_K_Flip_Flop j_k_ff_3 (.J(or_5_out), .clk(CLK), .K(or_6_out), .Q(OUTPUT[2]), .reset(CLR));  // open: Qn, preset, en
  J_K_Flip_Flop j_k_ff_4 (.J(or_7_out), .clk(CLK), .K(or_8_out), .Q(OUTPUT[3]), .reset(CLR));  // open: Qn, preset, en
endmodule

module _8_bit_register (
  input  LD,
  input  [7:0] in_2,
  input  CLK,
  output [7:0] out_4
);

  _4_bit_register u_4_bit_register_1 (.INPUT(in_2[3:0]), .CLK(CLK), .OUTPUT(out_4[3:0]), .LD(LD));  // open: INC, CLR
  _4_bit_register u_4_bit_register_2 (.INPUT(in_2[7:4]), .CLK(CLK), .OUTPUT(out_4[7:4]), .LD(LD));  // open: INC, CLR
endmodule
